# Fritzing sketch DIY-Lego-Controller (saved by Fritzing 1.0.5)
circuit board: 5cm x 7cm
perfboards: 1

parts:
  OLED-SSD_1306 = OLED 128x64 I2C Monochrome Display
  04 = Dagu DGServo 9g header (male) [package=THT]
  02 = Dagu DGServo 9g header (male) [package=THT]
  13 = Dagu DGServo 9g header (male) [package=THT]
  Serial_5V|GND|TX|TR|3_3V = male pin header, 5 pins [form="♂ (male)"]
  5V_|_GND = female pin header, 2 pins [form="♀ (female)"]
  OFF_|_ON = SPST Switch [package=switch-spdt_lock.007s]
  ESP32CAM = ESP32 - CAM
  14 = Dagu DGServo 9g header (male) [package=THT]
  15 = Dagu DGServo 9g header (male) [package=THT]
  12 = Dagu DGServo 9g header (male) [package=THT]
  GND|VDD|SDA|SCK_I²C = male pin header, 4 pins [form="♂ (male)"]
  3_3V_|_5V = SPST Switch [package=switch-spdt_lock.007s]
  flash_|_boot = SPST Switch [package=switch-spdt_lock.007s]
  C = Capacitor Polarized [package=cpol-radial-100uf-25v]

nets:
  GND: OLED-SSD_1306.GND, 04.gnd, 02.gnd, 13.gnd, Serial_5V|GND|TX|TR|3_3V.pin4, 5V_|_GND.pin2, ESP32CAM.GND, 14.gnd, 15.gnd, 12.gnd, GND|VDD|SDA|SCK_I²C.pin4, flash_|_boot.S, C.-
  N1: OLED-SSD_1306.VDD, GND|VDD|SDA|SCK_I²C.pin3, 3_3V_|_5V.P
  N2: OLED-SSD_1306.SCK, ESP32CAM.IO15, 15.pulse, GND|VDD|SDA|SCK_I²C.pin1
  N3: OLED-SSD_1306.SDA, ESP32CAM.IO14, 14.pulse, GND|VDD|SDA|SCK_I²C.pin2
  VCC: 04.Vcc, 02.Vcc, 13.Vcc, Serial_5V|GND|TX|TR|3_3V.pin5, OFF_|_ON.O, ESP32CAM.5V, ESP32CAM.VCC, 14.Vcc, 15.Vcc, 12.Vcc, 3_3V_|_5V.O, C.+
  N4: 04.pulse, ESP32CAM.IO4
  N5: 02.pulse, ESP32CAM.IO2
  N6: 13.pulse, ESP32CAM.IO13
  N7: Serial_5V|GND|TX|TR|3_3V.pin1, ESP32CAM.3V3, 3_3V_|_5V.S
  N8: Serial_5V|GND|TX|TR|3_3V.pin2, ESP32CAM.VOR
  N9: Serial_5V|GND|TX|TR|3_3V.pin3, ESP32CAM.VOT
  N10: 5V_|_GND.pin1, OFF_|_ON.P
  N11: ESP32CAM.IO12, 12.pulse
  N12: ESP32CAM.IO0, flash_|_boot.P

custom parts:
  ESP32 - CAM: The ESP32-CAM has a very competitive small-size camera module that can operate independently as a minimum system with a footprint of only 27*40.5*4.5mm and a deep sleep current of up to 6mA.
