# Fritzing sketch Lego-Driver (saved by Fritzing 1.0.5)
circuit board: 6cm x 4cm
perfboards: 1

parts:
  OLED_SSD1306 = OLED 128x64 I2C Monochrome Display
  M1 = Dagu DGServo 9g (Pan and tilt) [part_number=RS001B]
  M2 = Dagu DGServo 9g (Pan and tilt) [part_number=RS001B]
  M3 = Dagu DGServo 9g (Pan and tilt) [part_number=RS001B]
  M4 = Dagu DGServo 9g (Pan and tilt) [part_number=RS001B]
  ESP32-CAM = ESP32 - CAM
  J1 = female pin header, 4 pins [form="♀ (female)"]
  J2 = female pin header, 4 pins [form="♀ (female)"]
  J3 = female pin header, 4 pins [form="♀ (female)"]
  Power = female pin header, 2 pins [form="♀ (female)"]
  Power1 = female pin header, 2 pins [form="♀ (female)"]

nets:
  GND: OLED_SSD1306.GND, ESP32-CAM.GND, J1.pin2, J2.pin2, J3.pin2, Power.pin1, Power1.pin1
  VDD: OLED_SSD1306.VDD, ESP32-CAM.5V, J1.pin1, J2.pin1, J3.pin1, Power.pin2, Power1.pin2
  N1: OLED_SSD1306.SCK, ESP32-CAM.IO14, J1.pin3, J2.pin3, J3.pin3
  N2: OLED_SSD1306.SDA, ESP32-CAM.IO15, J1.pin4, J2.pin4, J3.pin4
  GND_2: M1.gnd, M2.gnd, M3.gnd, M4.gnd
  VCC: M1.vcc, M2.vcc, M3.vcc, M4.vcc
  N3: M1.pulse, ESP32-CAM.IO12
  N4: M2.pulse, ESP32-CAM.IO13
  N5: M3.pulse, ESP32-CAM.IO2
  N6: M4.pulse, ESP32-CAM.IO4

custom parts:
  ESP32 - CAM: The ESP32-CAM has a very competitive small-size camera module that can operate independently as a minimum system with a footprint of only 27*40.5*4.5mm and a deep sleep current of up to 6mA.
