# Fritzing sketch DIY-Lego-Controller (saved by Fritzing 1.0.5)
circuit board: 6.93215cm x 5.58306cm
perfboards: 1

parts:
  ESP32CAM = ESP32 - CAM
  OLED1 = OLED 128x64 I2C Monochrome Display
  J1 = Dagu DGServo 9g header (male) [package=THT]
  J2 = Dagu DGServo 9g header (male) [package=THT]
  J3 = Dagu DGServo 9g header (male) [package=THT]
  J4 = Dagu DGServo 9g header (male) [package=THT]
  Serial-Interface = male pin header, 5 pins [form="♂ (male)"]
  Boot_Switch = SPST Switch [package=switch-spdt_lock.007s]
  I2C-Interface = male pin header, 4 pins [form="♂ (male)"]
  Power_1 = male pin header, 2 pins [form="♂ (male)"]  # not connected
  J5 = female pin header, 2 pins [form="♀ (female)"]  # not connected

nets (from the pcb view):
  VCC: ESP32CAM.5V, OLED1.VDD, J1.Vcc, J2.Vcc, J3.Vcc, J4.Vcc, Serial-Interface.pin5
  GND: ESP32CAM.GND, OLED1.GND, J4.gnd, Serial-Interface.pin4, Boot_Switch.S, I2C-Interface.pin2
  N1: ESP32CAM.IO13, J3.pulse
  N2: ESP32CAM.IO15, OLED1.SCK
  N3: ESP32CAM.IO14, OLED1.SDA
  N4: ESP32CAM.IO2, J2.pulse
  N5: ESP32CAM.IO4, J1.pulse
  N6: ESP32CAM.VOT, Serial-Interface.pin3
  N7: ESP32CAM.VOR, Serial-Interface.pin2
  N8: ESP32CAM.IO0, Boot_Switch.P
  N9: ESP32CAM.3V3, Serial-Interface.pin1
  GND_2: J1.gnd, J2.gnd, J3.gnd

custom parts:
  ESP32 - CAM: The ESP32-CAM has a very competitive small-size camera module that can operate independently as a minimum system with a footprint of only 27*40.5*4.5mm and a deep sleep current of up to 6mA.
